# Fritzing sketch anolog-pins-as-input-potentiometer (saved by Fritzing 0.9.3b)

parts:
  Part1 = Arduino Uno (Rev3) - ICSP
  S2 = Square Pushbutton
  R1 = Resistor [tolerance=±5% resistance=220 package=THT]

nets:
  N1: Part1.GND, S2.leg0
  N2: Part1.D5_PWM, S2.leg1, R1.Pin_0
  N3: Part1.5V, R1.Pin_1
