# Fritzing sketch serial-communication-UART (saved by Fritzing 0.9.3b)

parts:
  Part2 = Arduino Uno (Rev3) - ICSP
  LED1 = LED - 5mm [color="Red (633nm)" package="5 mm [THT]"]
  R1 = Resistor [tolerance=±5% resistance=220 package=THT]

nets:
  N1: Part2.D8, R1.Pin_1
  N2: Part2.GND, LED1.cathode
  N3: LED1.anode, R1.Pin_0

notes:
  Serial Monitor
