# Fritzing sketch dht22-example (saved by Fritzing 0.9.3b)
breadboards: 1

parts:
  DHT1 = DHT22 Humidity and Temperature Sensor
  Part1 = Arduino Uno (Rev3) - ICSP
  R1 = Resistor [tolerance=±5% resistance=220 package=THT]

nets:
  VDD: DHT1.VDD, Part1.5V, R1.Pin_0
  N1: DHT1.DATA, Part1.D2, R1.Pin_1
  GND: DHT1.GND, Part1.GND

notes:
  10KOhm
  DHT22
