# Fritzing sketch thermistor-circuit (saved by Fritzing 0.9.3b)
breadboards: 1

parts:
  R1 = Temperature Sensor (Thermistor) [thermistor_type=NTC package=THT]
  R2 = Resistor [tolerance=±5% resistance=220 package=THT]
  Part1 = Arduino Uno (Rev3) - ICSP

nets:
  N1: R1.pin_0, R2.Pin_0, Part1.A0
  N2: R1.pin_1, Part1.GND
  N3: R2.Pin_1, Part1.5V

notes:
  Thermistor 20KOhm
  Resistor 20KOhm
